# Fritzing sketch boxty_wiring (saved by Fritzing 0.9.3b)
breadboards: 1

parts:
  Raspberry_Pi_1 = Raspberry Pi 3 [part_number=RPI-3-V1.2]
  LED1 = smd LED [color="Red (633nm)" package="0805 [SMD]"]
  LED2 = smd LED [color="Red (633nm)" package="0805 [SMD]"]
  R1 = Resistor [tolerance=±5% resistance=220 package="1206 [SMD]"]
  R2 = Resistor [tolerance=±5% resistance=220 package="1206 [SMD]"]
  J1 = Piezo Speaker
  J2 = Basic Servo
  PIR1 = PIR_sensor

nets:
  GND: Raspberry_Pi_1.GND, R1.Pin_0, R2.Pin_0, J1.pin1, J2.gnd, PIR1.connector3
  N1: Raspberry_Pi_1.GIPO9, PIR1.connector2
  N2: Raspberry_Pi_1.GIPO5, J2.pulse
  N3: Raspberry_Pi_1.GIPO6, LED2.anode
  N4: Raspberry_Pi_1.GIPO13, LED1.anode
  N5: Raspberry_Pi_1.GIPO26, J1.pin2
  5V: Raspberry_Pi_1.5V, J2.vcc, PIR1.connector1
  N6: LED1.cathode, R2.Pin_1
  N7: LED2.cathode, R1.Pin_1

notes:
  Eyes
  Rotates robot's head
  Beeps when servo limit is reached
  Checks for motion for 60 seconds.
